// Logisim project 16BitCPU.circ as structural Verilog: 1 circuit, main circuit main
module main (
);

  wire A_IN, A_OUT, ALU_OUT, B_IN, B_OUT, CARRY_FLAG, CLK, counter_2_carry, decoder_1_out0, decoder_1_out1,
       decoder_1_out2, decoder_1_out3, decoder_1_out4, decoder_1_out5, decoder_1_out6, decoder_1_out7,
       INST_IN, not_1_out, PC_ENABLE, PC_IN, PC_OUT, PC_RESET, pull_resistor_1_node, pull_resistor_2_node,
       RAM_ADDR, RAM_IN, RAM_OUT, RST, ZERO_FLAG;
  wire [3:0] ALU_NIBBLE_1, ALU_NIBBLE_2, ALU_NIBBLE_3, ALU_NIBBLE_4;
  wire [6:0] register_4_q_3, register_5_q;
  wire [7:0] counter_2_q, counter_3_q;
  wire [7:4] rom_2_data, rom_3_data, rom_4_data;
  wire [7:5] rom_1_data;
  wire [9:0] counter_1_q;
  wire [11:0] register_4_q;
  wire [12:0] register_4_q_2;
  wire [15:0] MAIN_BUS, ram_1_dout, register_1_q, register_2_q;

  not not_1 (not_1_out, CLK);
  Register #(.width(16)) register_1 (
    .D(MAIN_BUS), .en(RAM_ADDR), .Q(register_1_q), .clk(CLK), .clr(pull_resistor_1_node));
  Pull_Resistor pull_resistor_1 (.node(pull_resistor_1_node));
  Register #(.width(16)) register_2 (
    .D(MAIN_BUS), .en(RAM_IN), .Q(register_2_q), .clk(CLK), .clr(pull_resistor_2_node));
  Pull_Resistor pull_resistor_2 (.node(pull_resistor_2_node));
  RAM #(.addrWidth(16), .dataWidth(16), .trigger("high")) ram_1 (
    .addr(register_1_q), .we(RAM_IN), .oe(RAM_OUT), .din(register_2_q), .dout(ram_1_dout));
  Register #(.width(6)) register_3 (.D(MAIN_BUS[5:0]), .en(INST_IN), .clk(CLK), .Q(counter_1_q[5:0]));  // open: clr
  Counter #(.max('hf), .width(4)) counter_1 (
    .Q(counter_1_q[9:6]), .up(1'b1), .clk(not_1_out));  // open: load, D, count, carry, clr
  Hex_Digit_Display hex_digit_display_1 (.value(counter_1_q[9:6]));  // open: dp
  assign MAIN_BUS = RAM_OUT ? ram_1_dout : 16'bz;  // Controlled_Buffer controlled_buffer_1
  LED led_1 (.in(MAIN_BUS[15]));
  LED led_2 (.in(MAIN_BUS[14]));
  LED led_3 (.in(MAIN_BUS[13]));
  LED led_4 (.in(MAIN_BUS[12]));
  LED led_5 (.in(MAIN_BUS[11]));
  LED led_6 (.in(MAIN_BUS[10]));
  Clock clock_1 (.out(CLK));
  LED led_7 (.in(MAIN_BUS[9]));
  LED led_8 (.in(MAIN_BUS[8]));
  LED led_9 (.in(MAIN_BUS[7]));
  LED led_10 (.in(MAIN_BUS[6]));
  LED led_11 (.in(MAIN_BUS[5]));
  LED led_12 (.in(MAIN_BUS[4]));
  LED led_13 (.in(MAIN_BUS[3]));
  LED led_14 (.in(MAIN_BUS[2]));
  Pull_Resistor pull_resistor_3 (.node(MAIN_BUS));
  LED led_15 (.in(MAIN_BUS[1]));
  LED led_16 (.in(MAIN_BUS[0]));
  Pull_Resistor pull_resistor_4 (.node(RAM_IN));
  Pull_Resistor pull_resistor_5 (.node(RAM_OUT));
  Pull_Resistor pull_resistor_6 (.node(PC_ENABLE));
  Pull_Resistor pull_resistor_7 (.node(PC_RESET));
  Pull_Resistor pull_resistor_8 (.node(PC_IN));
  Pull_Resistor pull_resistor_9 (.node(PC_OUT));
  Counter counter_2 (
    .load(PC_IN), .D(MAIN_BUS[7:0]), .count(PC_ENABLE), .Q(counter_2_q), .carry(counter_2_carry), .up(1'b1),
    .clk(CLK), .clr(PC_RESET));
  assign MAIN_BUS[7:0] = PC_OUT ? counter_2_q : 8'bz;  // Controlled_Buffer controlled_buffer_2
  assign MAIN_BUS[15:8] = PC_OUT ? counter_3_q : 8'bz;  // Controlled_Buffer controlled_buffer_3
  Counter counter_3 (
    .load(PC_IN), .D(MAIN_BUS[15:8]), .count(counter_2_carry), .Q(counter_3_q), .up(1'b1), .clk(CLK),
    .clr(PC_RESET));  // open: carry
  ROM #(.addrWidth(13)) rom_1 (
    .addr({register_4_q_2[12:8], 3'b000, register_4_q_2[4:0]}), .data({rom_1_data, CARRY_FLAG, ALU_NIBBLE_4}));
  and and_1 (ZERO_FLAG, ALU_NIBBLE_1[0], ALU_NIBBLE_1[1], ALU_NIBBLE_1[2], ALU_NIBBLE_1[3], ALU_NIBBLE_2[0], ALU_NIBBLE_2[1], ALU_NIBBLE_2[2], ALU_NIBBLE_2[3], ALU_NIBBLE_3[0], ALU_NIBBLE_3[1], ALU_NIBBLE_3[2], ALU_NIBBLE_3[3], ALU_NIBBLE_4[0], ALU_NIBBLE_4[1], ALU_NIBBLE_4[2], ALU_NIBBLE_4[3]);
  DipSwitch #(.number(24)) dipswitch_1 (
    .sw20(A_IN), .sw21(A_OUT), .sw22(B_IN), .sw23(B_OUT), .sw24(ALU_OUT));  // open: sw1, sw2, sw3, sw4, sw5, sw6, sw7, sw8, sw9, sw10, sw11, sw12, sw13, sw14, sw15, sw16, sw17, sw18, sw19
  assign MAIN_BUS = ALU_OUT ? {ALU_NIBBLE_4, ALU_NIBBLE_3, ALU_NIBBLE_2, ALU_NIBBLE_1} : 16'bz;  // Controlled_Buffer controlled_buffer_4
  Decoder #(.enable("false"), .select(3)) decoder_1 (
    .out0(decoder_1_out0), .out1(decoder_1_out1), .out2(decoder_1_out2), .out3(decoder_1_out3),
    .out4(decoder_1_out4), .out5(decoder_1_out5), .out6(decoder_1_out6), .out7(decoder_1_out7), .sel(3'b000));
  ROM #(.addrWidth(13)) rom_2 (
    .addr({register_4_q_2[8], register_4_q[11:8], 3'b000, register_4_q_2[0], register_4_q[3:0]}),
    .data({rom_2_data, ALU_NIBBLE_3}));
  Register #(.width(16)) register_4 (
    .D(MAIN_BUS), .en(A_IN), .clk(CLK), .Q({register_4_q_2[4:0], register_4_q[3:0], register_4_q_3}),
    .clr(RST));
  LED led_17 (.in(decoder_1_out0));
  LED led_18 (.in(decoder_1_out1));
  LED led_19 (.in(decoder_1_out2));
  LED led_20 (.in(decoder_1_out3));
  LED led_21 (.in(decoder_1_out4));
  LED led_22 (.in(decoder_1_out5));
  LED led_23 (.in(decoder_1_out6));
  LED led_24 (.in(decoder_1_out7));
  Register #(.width(16)) register_5 (
    .D(MAIN_BUS), .en(B_IN), .clk(CLK), .Q({register_4_q_2[12:8], register_4_q[11:8], register_5_q}),
    .clr(RST));
  assign MAIN_BUS = A_OUT ? {register_4_q_2[4:0], register_4_q[3:0], register_4_q_3} : 16'bz;  // Controlled_Buffer controlled_buffer_5
  assign MAIN_BUS = B_OUT ? {register_4_q_2[12:8], register_4_q[11:8], register_5_q} : 16'bz;  // Controlled_Buffer controlled_buffer_6
  ROM #(.addrWidth(13)) rom_3 (
    .addr({register_4_q[8], register_5_q[6:3], 3'b000, register_4_q[0], register_4_q_3[6:3]}),
    .data({rom_3_data, ALU_NIBBLE_2}));
  Pull_Resistor pull_resistor_10 (.node(RST));
  ROM #(.addrWidth(13)) rom_4 (
    .addr({register_5_q[3:0], 4'b0000, register_4_q_3[3:0], 1'b0}), .data({rom_4_data, ALU_NIBBLE_1}));

  // Notes on the sheet:
  //   Program Counter - 16Bit
  //   contents of rom_1 (hex, n*v repeats v):
  //   0 0 1 1 2 2 3 3 4 4 5 5 6 6 7 7 8 8 9 9 a a b b c c d d e e f f 0 0 1 1 2 2 3 3 4 4 5 5 6 6 7 7 8 8
  //   9 9 a a b b c c d d e e f f 34*0 1 1 2 2 3 3 4 4 5 5 6 6 7 7 8 8 9 9 a a b b c c d d e e f f 0 0 1 1
  //   2 2 3 3 4 4 5 5 6 6 7 7 8 8 9 9 a a b b c c d d e e f f 0 1 2 3 4 5 6 7 8 9 a b c d e f 0 1 2 3 4 5
  //   6 7 8 9 a b c d e f 65*0 1 1 2 2 3 3 4 4 5 5 6 6 7 7 8 8 9 9 a a b b c c d d e e f f 10 f 10 10 11
  //   11 12 12 13 13 14 14 15 15 16 16 17 17 18 18 19 19 1a 1a 1b 1b 1c 1c 1d 1d 1e 1e 1f 34*0 1 1 2 2 3 3
  //   4 4 5 5 6 6 7 7 8 8 9 9 a a b b c c d d e e f f 0 0 1 1 2 2 3 3 4 4 5 5 6 6 7 7 8 8 9 9 a a b b c c
  //   d d e e f f 0 1 2 3 4 5 6 7 8 9 a b c d e f 0 1 2 3 4 5 6 7 8 9 a b c d e f 32*1 32*0 1 1 2 2 3 3 4
  //   4 5 5 6 6 7 7 8 8 9 9 a a b b c c d d e e f f 10 10 f f 10 10 11 11 12 12 13 13 14 14 15 15 16 16 17
  //   17 18 18 19 19 1a 1a 1b 1b 1c 1c 1d 1d 1e 1e 0 0 1 1 0 0 1 1 0 0 1 1 0 0 1 1 0 0 1 1 0 0 1 1 0 0 1 1
  //   0 0 6*1 4*3 4*5 4*7 4*9 4*b 4*d 4*f 1 1 0 0 3 3 2 2 5 5 4 4 7 7 6 6 9 9 8 8 b b a a d d c c f f e e
  //   0 1 2 3 4 5 6 7 8 9 a b c d e f 0 1 2 3 4 5 6 7 8 9 a b c d e f 32*2 32*0 1 2 2 3 3 4 4 5 5 6 6 7 7
  //   8 8 9 9 a a b b c c d d e e f f 10 10 11 e f f 10 10 11 11 12 12 13 13 14 14 15 15 16 16 17 17 18 18
  //   19 19 1a 1a 1b 1b 1c 1c 1d 1d 1e 0 0 1 1 0 0 1 1 0 0 1 1 0 0 1 1 0 0 1 1 0 0 1 1 0 0 1 1 0 0 6*1 4*3
  //   4*5 4*7 4*9 4*b 4*d 4*f 1 1 0 0 3 3 2 2 5 5 4 4 7 7 6 6 9 9 8 8 b b a a d d c c f f e e 0 1 2 3 4 5
  //   6 7 8 9 a b c d e f 0 1 2 3 4 5 6 7 8 9 a b c d e f 32*3 32*0 2 2 3 3 4 4 5 5 6 6 7 7 8 8 9 9 a a b
  //   b c c d d e e f f 10 10 11 11 e e f f 10 10 11 11 12 12 13 13 14 14 15 15 16 16 17 17 18 18 19 19 1a
  //   1a 1b 1b 1c 1c 1d 1d 4*0 4*2 4*0 4*2 4*0 4*2 4*0 6*2 3 3 2 2 3 3 6 6 7 7 6 6 7 7 a a b b a a b b e e
  //   f f e e f f 2 2 3 3 0 0 1 1 6 6 7 7 4 4 5 5 a a b b 8 8 9 9 e e f f c c d d 0 1 2 3 4 5 6 7 8 9 a b
  //   c d e f 0 1 2 3 4 5 6 7 8 9 a b c d e f 32*4 32*0 2 3 3 4 4 5 5 6 6 7 7 8 8 9 9 a a b b c c d d e e
  //   f f 10 10 11 11 12 d e e f f 10 10 11 11 12 12 13 13 14 14 15 15 16 16 17 17 18 18 19 19 1a 1a 1b 1b
  //   1c 1c 1d 4*0 4*2 4*0 4*2 4*0 4*2 4*0 6*2 3 3 2 2 3 3 6 6 7 7 6 6 7 7 a a b b a a b b e e f f e e f f
  //   2 2 3 3 0 0 1 1 6 6 7 7 4 4 5 5 a a b b 8 8 9 9 e e f f c c d d 0 1 2 3 4 5 6 7 8 9 a b c d e f 0 1
  //   2 3 4 5 6 7 8 9 a b c d e f 32*5 32*0 3 3 4 4 5 5 6 6 7 7 8 8 9 9 a a b b c c d d e e f f 10 10 11
  //   11 12 12 d d e e f f 10 10 11 11 12 12 13 13 14 14 15 15 16 16 17 17 18 18 19 19 1a 1a 1b 1b 1c 1c 0
  //   0 1 1 2 2 3 3 0 0 1 1 2 2 3 3 0 0 1 1 2 2 3 3 0 0 1 1 2 2 10*3 8*7 8*b 8*f 3 3 2 2 1 1 0 0 7 7 6 6 5
  //   5 4 4 b b a a 9 9 8 8 f f e e d d c c 0 1 2 3 4 5 6 7 8 9 a b c d e f 0 1 2 3 4 5 6 7 8 9 a b c d e
  //   f 32*6 32*0 3 4 4 5 5 6 6 7 7 8 8 9 9 a a b b c c d d e e f f 10 10 11 11 12 12 13 c d d e e f f 10
  //   10 11 11 12 12 13 13 14 14 15 15 16 16 17 17 18 18 19 19 1a 1a 1b 1b 1c 0 0 1 1 2 2 3 3 0 0 1 1 2 2
  //   3 3 0 0 1 1 2 2 3 3 0 0 1 1 2 2 10*3 8*7 8*b 8*f 3 3 2 2 1 1 0 0 7 7 6 6 5 5 4 4 b b a a 9 9 8 8 f f
  //   e e d d c c 0 1 2 3 4 5 6 7 8 9 a b c d e f 0 1 2 3 4 5 6 7 8 9 a b c d e f 32*7 32*0 4 4 5 5 6 6 7
  //   7 8 8 9 9 a a b b c c d d e e f f 10 10 11 11 12 12 13 13 c c d d e e f f 10 10 11 11 12 12 13 13 14
  //   14 15 15 16 16 17 17 18 18 19 19 1a 1a 1b 1b 8*0 8*4 8*0 10*4 5 5 6 6 7 7 4 4 5 5 6 6 7 7 c c d d e
  //   e f f c c d d e e f f 4 4 5 5 6 6 7 7 0 0 1 1 2 2 3 3 c c d d e e f f 8 8 9 9 a a b b 0 1 2 3 4 5 6
  //   7 8 9 a b c d e f 0 1 2 3 4 5 6 7 8 9 a b c d e f 32*8 32*0 4 5 5 6 6 7 7 8 8 9 9 a a b b c c d d e
  //   e f f 10 10 11 11 12 12 13 13 14 b c c d d e e f f 10 10 11 11 12 12 13 13 14 14 15 15 16 16 17 17
  //   18 18 19 19 1a 1a 1b 8*0 8*4 8*0 10*4 5 5 6 6 7 7 4 4 5 5 6 6 7 7 c c d d e e f f c c d d e e f f 4
  //   4 5 5 6 6 7 7 0 0 1 1 2 2 3 3 c c d d e e f f 8 8 9 9 a a b b 0 1 2 3 4 5 6 7 8 9 a b c d e f 0 1 2
  //   3 4 5 6 7 8 9 a b c d e f 32*9 32*0 5 5 6 6 7 7 8 8 9 9 a a b b c c d d e e f f 10 10 11 11 12 12 13
  //   13 14 14 b b c c d d e e f f 10 10 11 11 12 12 13 13 14 14 15 15 16 16 17 17 18 18 19 19 1a 1a 0 0 1
  //   1 0 0 1 1 4 4 5 5 4 4 5 5 0 0 1 1 0 0 1 1 4 4 5 5 4 4 6*5 4*7 4*5 4*7 4*d 4*f 4*d 4*f 5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
  //   contents of rom_2 (hex, n*v repeats v):
  //   0 0 1 1 2 2 3 3 4 4 5 5 6 6 7 7 8 8 9 9 a a b b c c d d e e f f 0 0 1 1 2 2 3 3 4 4 5 5 6 6 7 7 8 8
  //   9 9 a a b b c c d d e e f f 34*0 1 1 2 2 3 3 4 4 5 5 6 6 7 7 8 8 9 9 a a b b c c d d e e f f 0 0 1 1
  //   2 2 3 3 4 4 5 5 6 6 7 7 8 8 9 9 a a b b c c d d e e f f 0 1 2 3 4 5 6 7 8 9 a b c d e f 0 1 2 3 4 5
  //   6 7 8 9 a b c d e f 65*0 1 1 2 2 3 3 4 4 5 5 6 6 7 7 8 8 9 9 a a b b c c d d e e f f 10 f 10 10 11
  //   11 12 12 13 13 14 14 15 15 16 16 17 17 18 18 19 19 1a 1a 1b 1b 1c 1c 1d 1d 1e 1e 1f 34*0 1 1 2 2 3 3
  //   4 4 5 5 6 6 7 7 8 8 9 9 a a b b c c d d e e f f 0 0 1 1 2 2 3 3 4 4 5 5 6 6 7 7 8 8 9 9 a a b b c c
  //   d d e e f f 0 1 2 3 4 5 6 7 8 9 a b c d e f 0 1 2 3 4 5 6 7 8 9 a b c d e f 32*1 32*0 1 1 2 2 3 3 4
  //   4 5 5 6 6 7 7 8 8 9 9 a a b b c c d d e e f f 10 10 f f 10 10 11 11 12 12 13 13 14 14 15 15 16 16 17
  //   17 18 18 19 19 1a 1a 1b 1b 1c 1c 1d 1d 1e 1e 0 0 1 1 0 0 1 1 0 0 1 1 0 0 1 1 0 0 1 1 0 0 1 1 0 0 1 1
  //   0 0 6*1 4*3 4*5 4*7 4*9 4*b 4*d 4*f 1 1 0 0 3 3 2 2 5 5 4 4 7 7 6 6 9 9 8 8 b b a a d d c c f f e e
  //   0 1 2 3 4 5 6 7 8 9 a b c d e f 0 1 2 3 4 5 6 7 8 9 a b c d e f 32*2 32*0 1 2 2 3 3 4 4 5 5 6 6 7 7
  //   8 8 9 9 a a b b c c d d e e f f 10 10 11 e f f 10 10 11 11 12 12 13 13 14 14 15 15 16 16 17 17 18 18
  //   19 19 1a 1a 1b 1b 1c 1c 1d 1d 1e 0 0 1 1 0 0 1 1 0 0 1 1 0 0 1 1 0 0 1 1 0 0 1 1 0 0 1 1 0 0 6*1 4*3
  //   4*5 4*7 4*9 4*b 4*d 4*f 1 1 0 0 3 3 2 2 5 5 4 4 7 7 6 6 9 9 8 8 b b a a d d c c f f e e 0 1 2 3 4 5
  //   6 7 8 9 a b c d e f 0 1 2 3 4 5 6 7 8 9 a b c d e f 32*3 32*0 2 2 3 3 4 4 5 5 6 6 7 7 8 8 9 9 a a b
  //   b c c d d e e f f 10 10 11 11 e e f f 10 10 11 11 12 12 13 13 14 14 15 15 16 16 17 17 18 18 19 19 1a
  //   1a 1b 1b 1c 1c 1d 1d 4*0 4*2 4*0 4*2 4*0 4*2 4*0 6*2 3 3 2 2 3 3 6 6 7 7 6 6 7 7 a a b b a a b b e e
  //   f f e e f f 2 2 3 3 0 0 1 1 6 6 7 7 4 4 5 5 a a b b 8 8 9 9 e e f f c c d d 0 1 2 3 4 5 6 7 8 9 a b
  //   c d e f 0 1 2 3 4 5 6 7 8 9 a b c d e f 32*4 32*0 2 3 3 4 4 5 5 6 6 7 7 8 8 9 9 a a b b c c d d e e
  //   f f 10 10 11 11 12 d e e f f 10 10 11 11 12 12 13 13 14 14 15 15 16 16 17 17 18 18 19 19 1a 1a 1b 1b
  //   1c 1c 1d 4*0 4*2 4*0 4*2 4*0 4*2 4*0 6*2 3 3 2 2 3 3 6 6 7 7 6 6 7 7 a a b b a a b b e e f f e e f f
  //   2 2 3 3 0 0 1 1 6 6 7 7 4 4 5 5 a a b b 8 8 9 9 e e f f c c d d 0 1 2 3 4 5 6 7 8 9 a b c d e f 0 1
  //   2 3 4 5 6 7 8 9 a b c d e f 32*5 32*0 3 3 4 4 5 5 6 6 7 7 8 8 9 9 a a b b c c d d e e f f 10 10 11
  //   11 12 12 d d e e f f 10 10 11 11 12 12 13 13 14 14 15 15 16 16 17 17 18 18 19 19 1a 1a 1b 1b 1c 1c 0
  //   0 1 1 2 2 3 3 0 0 1 1 2 2 3 3 0 0 1 1 2 2 3 3 0 0 1 1 2 2 10*3 8*7 8*b 8*f 3 3 2 2 1 1 0 0 7 7 6 6 5
  //   5 4 4 b b a a 9 9 8 8 f f e e d d c c 0 1 2 3 4 5 6 7 8 9 a b c d e f 0 1 2 3 4 5 6 7 8 9 a b c d e
  //   f 32*6 32*0 3 4 4 5 5 6 6 7 7 8 8 9 9 a a b b c c d d e e f f 10 10 11 11 12 12 13 c d d e e f f 10
  //   10 11 11 12 12 13 13 14 14 15 15 16 16 17 17 18 18 19 19 1a 1a 1b 1b 1c 0 0 1 1 2 2 3 3 0 0 1 1 2 2
  //   3 3 0 0 1 1 2 2 3 3 0 0 1 1 2 2 10*3 8*7 8*b 8*f 3 3 2 2 1 1 0 0 7 7 6 6 5 5 4 4 b b a a 9 9 8 8 f f
  //   e e d d c c 0 1 2 3 4 5 6 7 8 9 a b c d e f 0 1 2 3 4 5 6 7 8 9 a b c d e f 32*7 32*0 4 4 5 5 6 6 7
  //   7 8 8 9 9 a a b b c c d d e e f f 10 10 11 11 12 12 13 13 c c d d e e f f 10 10 11 11 12 12 13 13 14
  //   14 15 15 16 16 17 17 18 18 19 19 1a 1a 1b 1b 8*0 8*4 8*0 10*4 5 5 6 6 7 7 4 4 5 5 6 6 7 7 c c d d e
  //   e f f c c d d e e f f 4 4 5 5 6 6 7 7 0 0 1 1 2 2 3 3 c c d d e e f f 8 8 9 9 a a b b 0 1 2 3 4 5 6
  //   7 8 9 a b c d e f 0 1 2 3 4 5 6 7 8 9 a b c d e f 32*8 32*0 4 5 5 6 6 7 7 8 8 9 9 a a b b c c d d e
  //   e f f 10 10 11 11 12 12 13 13 14 b c c d d e e f f 10 10 11 11 12 12 13 13 14 14 15 15 16 16 17 17
  //   18 18 19 19 1a 1a 1b 8*0 8*4 8*0 10*4 5 5 6 6 7 7 4 4 5 5 6 6 7 7 c c d d e e f f c c d d e e f f 4
  //   4 5 5 6 6 7 7 0 0 1 1 2 2 3 3 c c d d e e f f 8 8 9 9 a a b b 0 1 2 3 4 5 6 7 8 9 a b c d e f 0 1 2
  //   3 4 5 6 7 8 9 a b c d e f 32*9 32*0 5 5 6 6 7 7 8 8 9 9 a a b b c c d d e e f f 10 10 11 11 12 12 13
  //   13 14 14 b b c c d d e e f f 10 10 11 11 12 12 13 13 14 14 15 15 16 16 17 17 18 18 19 19 1a 1a 0 0 1
  //   1 0 0 1 1 4 4 5 5 4 4 5 5 0 0 1 1 0 0 1 1 4 4 5 5 4 4 6*5 4*7 4*5 4*7 4*d 4*f 4*d 4*f 5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
  //   Register A - 16Bit
  //   DIV
  //   Register B - 16Bit
  //   ADD
  //   SUB
  //   AND
  //   OR
  //   XOR
  //   SHLA
  //   SHLB
  //   contents of rom_3 (hex, n*v repeats v):
  //   0 0 1 1 2 2 3 3 4 4 5 5 6 6 7 7 8 8 9 9 a a b b c c d d e e f f 0 0 1 1 2 2 3 3 4 4 5 5 6 6 7 7 8 8
  //   9 9 a a b b c c d d e e f f 34*0 1 1 2 2 3 3 4 4 5 5 6 6 7 7 8 8 9 9 a a b b c c d d e e f f 0 0 1 1
  //   2 2 3 3 4 4 5 5 6 6 7 7 8 8 9 9 a a b b c c d d e e f f 0 1 2 3 4 5 6 7 8 9 a b c d e f 0 1 2 3 4 5
  //   6 7 8 9 a b c d e f 65*0 1 1 2 2 3 3 4 4 5 5 6 6 7 7 8 8 9 9 a a b b c c d d e e f f 10 f 10 10 11
  //   11 12 12 13 13 14 14 15 15 16 16 17 17 18 18 19 19 1a 1a 1b 1b 1c 1c 1d 1d 1e 1e 1f 34*0 1 1 2 2 3 3
  //   4 4 5 5 6 6 7 7 8 8 9 9 a a b b c c d d e e f f 0 0 1 1 2 2 3 3 4 4 5 5 6 6 7 7 8 8 9 9 a a b b c c
  //   d d e e f f 0 1 2 3 4 5 6 7 8 9 a b c d e f 0 1 2 3 4 5 6 7 8 9 a b c d e f 32*1 32*0 1 1 2 2 3 3 4
  //   4 5 5 6 6 7 7 8 8 9 9 a a b b c c d d e e f f 10 10 f f 10 10 11 11 12 12 13 13 14 14 15 15 16 16 17
  //   17 18 18 19 19 1a 1a 1b 1b 1c 1c 1d 1d 1e 1e 0 0 1 1 0 0 1 1 0 0 1 1 0 0 1 1 0 0 1 1 0 0 1 1 0 0 1 1
  //   0 0 6*1 4*3 4*5 4*7 4*9 4*b 4*d 4*f 1 1 0 0 3 3 2 2 5 5 4 4 7 7 6 6 9 9 8 8 b b a a d d c c f f e e
  //   0 1 2 3 4 5 6 7 8 9 a b c d e f 0 1 2 3 4 5 6 7 8 9 a b c d e f 32*2 32*0 1 2 2 3 3 4 4 5 5 6 6 7 7
  //   8 8 9 9 a a b b c c d d e e f f 10 10 11 e f f 10 10 11 11 12 12 13 13 14 14 15 15 16 16 17 17 18 18
  //   19 19 1a 1a 1b 1b 1c 1c 1d 1d 1e 0 0 1 1 0 0 1 1 0 0 1 1 0 0 1 1 0 0 1 1 0 0 1 1 0 0 1 1 0 0 6*1 4*3
  //   4*5 4*7 4*9 4*b 4*d 4*f 1 1 0 0 3 3 2 2 5 5 4 4 7 7 6 6 9 9 8 8 b b a a d d c c f f e e 0 1 2 3 4 5
  //   6 7 8 9 a b c d e f 0 1 2 3 4 5 6 7 8 9 a b c d e f 32*3 32*0 2 2 3 3 4 4 5 5 6 6 7 7 8 8 9 9 a a b
  //   b c c d d e e f f 10 10 11 11 e e f f 10 10 11 11 12 12 13 13 14 14 15 15 16 16 17 17 18 18 19 19 1a
  //   1a 1b 1b 1c 1c 1d 1d 4*0 4*2 4*0 4*2 4*0 4*2 4*0 6*2 3 3 2 2 3 3 6 6 7 7 6 6 7 7 a a b b a a b b e e
  //   f f e e f f 2 2 3 3 0 0 1 1 6 6 7 7 4 4 5 5 a a b b 8 8 9 9 e e f f c c d d 0 1 2 3 4 5 6 7 8 9 a b
  //   c d e f 0 1 2 3 4 5 6 7 8 9 a b c d e f 32*4 32*0 2 3 3 4 4 5 5 6 6 7 7 8 8 9 9 a a b b c c d d e e
  //   f f 10 10 11 11 12 d e e f f 10 10 11 11 12 12 13 13 14 14 15 15 16 16 17 17 18 18 19 19 1a 1a 1b 1b
  //   1c 1c 1d 4*0 4*2 4*0 4*2 4*0 4*2 4*0 6*2 3 3 2 2 3 3 6 6 7 7 6 6 7 7 a a b b a a b b e e f f e e f f
  //   2 2 3 3 0 0 1 1 6 6 7 7 4 4 5 5 a a b b 8 8 9 9 e e f f c c d d 0 1 2 3 4 5 6 7 8 9 a b c d e f 0 1
  //   2 3 4 5 6 7 8 9 a b c d e f 32*5 32*0 3 3 4 4 5 5 6 6 7 7 8 8 9 9 a a b b c c d d e e f f 10 10 11
  //   11 12 12 d d e e f f 10 10 11 11 12 12 13 13 14 14 15 15 16 16 17 17 18 18 19 19 1a 1a 1b 1b 1c 1c 0
  //   0 1 1 2 2 3 3 0 0 1 1 2 2 3 3 0 0 1 1 2 2 3 3 0 0 1 1 2 2 10*3 8*7 8*b 8*f 3 3 2 2 1 1 0 0 7 7 6 6 5
  //   5 4 4 b b a a 9 9 8 8 f f e e d d c c 0 1 2 3 4 5 6 7 8 9 a b c d e f 0 1 2 3 4 5 6 7 8 9 a b c d e
  //   f 32*6 32*0 3 4 4 5 5 6 6 7 7 8 8 9 9 a a b b c c d d e e f f 10 10 11 11 12 12 13 c d d e e f f 10
  //   10 11 11 12 12 13 13 14 14 15 15 16 16 17 17 18 18 19 19 1a 1a 1b 1b 1c 0 0 1 1 2 2 3 3 0 0 1 1 2 2
  //   3 3 0 0 1 1 2 2 3 3 0 0 1 1 2 2 10*3 8*7 8*b 8*f 3 3 2 2 1 1 0 0 7 7 6 6 5 5 4 4 b b a a 9 9 8 8 f f
  //   e e d d c c 0 1 2 3 4 5 6 7 8 9 a b c d e f 0 1 2 3 4 5 6 7 8 9 a b c d e f 32*7 32*0 4 4 5 5 6 6 7
  //   7 8 8 9 9 a a b b c c d d e e f f 10 10 11 11 12 12 13 13 c c d d e e f f 10 10 11 11 12 12 13 13 14
  //   14 15 15 16 16 17 17 18 18 19 19 1a 1a 1b 1b 8*0 8*4 8*0 10*4 5 5 6 6 7 7 4 4 5 5 6 6 7 7 c c d d e
  //   e f f c c d d e e f f 4 4 5 5 6 6 7 7 0 0 1 1 2 2 3 3 c c d d e e f f 8 8 9 9 a a b b 0 1 2 3 4 5 6
  //   7 8 9 a b c d e f 0 1 2 3 4 5 6 7 8 9 a b c d e f 32*8 32*0 4 5 5 6 6 7 7 8 8 9 9 a a b b c c d d e
  //   e f f 10 10 11 11 12 12 13 13 14 b c c d d e e f f 10 10 11 11 12 12 13 13 14 14 15 15 16 16 17 17
  //   18 18 19 19 1a 1a 1b 8*0 8*4 8*0 10*4 5 5 6 6 7 7 4 4 5 5 6 6 7 7 c c d d e e f f c c d d e e f f 4
  //   4 5 5 6 6 7 7 0 0 1 1 2 2 3 3 c c d d e e f f 8 8 9 9 a a b b 0 1 2 3 4 5 6 7 8 9 a b c d e f 0 1 2
  //   3 4 5 6 7 8 9 a b c d e f 32*9 32*0 5 5 6 6 7 7 8 8 9 9 a a b b c c d d e e f f 10 10 11 11 12 12 13
  //   13 14 14 b b c c d d e e f f 10 10 11 11 12 12 13 13 14 14 15 15 16 16 17 17 18 18 19 19 1a 1a 0 0 1
  //   1 0 0 1 1 4 4 5 5 4 4 5 5 0 0 1 1 0 0 1 1 4 4 5 5 4 4 6*5 4*7 4*5 4*7 4*d 4*f 4*d 4*f 5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
  //   contents of rom_4 (hex, n*v repeats v):
  //   0 0 1 1 2 2 3 3 4 4 5 5 6 6 7 7 8 8 9 9 a a b b c c d d e e f f 0 0 1 1 2 2 3 3 4 4 5 5 6 6 7 7 8 8
  //   9 9 a a b b c c d d e e f f 34*0 1 1 2 2 3 3 4 4 5 5 6 6 7 7 8 8 9 9 a a b b c c d d e e f f 0 0 1 1
  //   2 2 3 3 4 4 5 5 6 6 7 7 8 8 9 9 a a b b c c d d e e f f 0 1 2 3 4 5 6 7 8 9 a b c d e f 0 1 2 3 4 5
  //   6 7 8 9 a b c d e f 65*0 1 1 2 2 3 3 4 4 5 5 6 6 7 7 8 8 9 9 a a b b c c d d e e f f 10 f 10 10 11
  //   11 12 12 13 13 14 14 15 15 16 16 17 17 18 18 19 19 1a 1a 1b 1b 1c 1c 1d 1d 1e 1e 1f 34*0 1 1 2 2 3 3
  //   4 4 5 5 6 6 7 7 8 8 9 9 a a b b c c d d e e f f 0 0 1 1 2 2 3 3 4 4 5 5 6 6 7 7 8 8 9 9 a a b b c c
  //   d d e e f f 0 1 2 3 4 5 6 7 8 9 a b c d e f 0 1 2 3 4 5 6 7 8 9 a b c d e f 32*1 32*0 1 1 2 2 3 3 4
  //   4 5 5 6 6 7 7 8 8 9 9 a a b b c c d d e e f f 10 10 f f 10 10 11 11 12 12 13 13 14 14 15 15 16 16 17
  //   17 18 18 19 19 1a 1a 1b 1b 1c 1c 1d 1d 1e 1e 0 0 1 1 0 0 1 1 0 0 1 1 0 0 1 1 0 0 1 1 0 0 1 1 0 0 1 1
  //   0 0 6*1 4*3 4*5 4*7 4*9 4*b 4*d 4*f 1 1 0 0 3 3 2 2 5 5 4 4 7 7 6 6 9 9 8 8 b b a a d d c c f f e e
  //   0 1 2 3 4 5 6 7 8 9 a b c d e f 0 1 2 3 4 5 6 7 8 9 a b c d e f 32*2 32*0 1 2 2 3 3 4 4 5 5 6 6 7 7
  //   8 8 9 9 a a b b c c d d e e f f 10 10 11 e f f 10 10 11 11 12 12 13 13 14 14 15 15 16 16 17 17 18 18
  //   19 19 1a 1a 1b 1b 1c 1c 1d 1d 1e 0 0 1 1 0 0 1 1 0 0 1 1 0 0 1 1 0 0 1 1 0 0 1 1 0 0 1 1 0 0 6*1 4*3
  //   4*5 4*7 4*9 4*b 4*d 4*f 1 1 0 0 3 3 2 2 5 5 4 4 7 7 6 6 9 9 8 8 b b a a d d c c f f e e 0 1 2 3 4 5
  //   6 7 8 9 a b c d e f 0 1 2 3 4 5 6 7 8 9 a b c d e f 32*3 32*0 2 2 3 3 4 4 5 5 6 6 7 7 8 8 9 9 a a b
  //   b c c d d e e f f 10 10 11 11 e e f f 10 10 11 11 12 12 13 13 14 14 15 15 16 16 17 17 18 18 19 19 1a
  //   1a 1b 1b 1c 1c 1d 1d 4*0 4*2 4*0 4*2 4*0 4*2 4*0 6*2 3 3 2 2 3 3 6 6 7 7 6 6 7 7 a a b b a a b b e e
  //   f f e e f f 2 2 3 3 0 0 1 1 6 6 7 7 4 4 5 5 a a b b 8 8 9 9 e e f f c c d d 0 1 2 3 4 5 6 7 8 9 a b
  //   c d e f 0 1 2 3 4 5 6 7 8 9 a b c d e f 32*4 32*0 2 3 3 4 4 5 5 6 6 7 7 8 8 9 9 a a b b c c d d e e
  //   f f 10 10 11 11 12 d e e f f 10 10 11 11 12 12 13 13 14 14 15 15 16 16 17 17 18 18 19 19 1a 1a 1b 1b
  //   1c 1c 1d 4*0 4*2 4*0 4*2 4*0 4*2 4*0 6*2 3 3 2 2 3 3 6 6 7 7 6 6 7 7 a a b b a a b b e e f f e e f f
  //   2 2 3 3 0 0 1 1 6 6 7 7 4 4 5 5 a a b b 8 8 9 9 e e f f c c d d 0 1 2 3 4 5 6 7 8 9 a b c d e f 0 1
  //   2 3 4 5 6 7 8 9 a b c d e f 32*5 32*0 3 3 4 4 5 5 6 6 7 7 8 8 9 9 a a b b c c d d e e f f 10 10 11
  //   11 12 12 d d e e f f 10 10 11 11 12 12 13 13 14 14 15 15 16 16 17 17 18 18 19 19 1a 1a 1b 1b 1c 1c 0
  //   0 1 1 2 2 3 3 0 0 1 1 2 2 3 3 0 0 1 1 2 2 3 3 0 0 1 1 2 2 10*3 8*7 8*b 8*f 3 3 2 2 1 1 0 0 7 7 6 6 5
  //   5 4 4 b b a a 9 9 8 8 f f e e d d c c 0 1 2 3 4 5 6 7 8 9 a b c d e f 0 1 2 3 4 5 6 7 8 9 a b c d e
  //   f 32*6 32*0 3 4 4 5 5 6 6 7 7 8 8 9 9 a a b b c c d d e e f f 10 10 11 11 12 12 13 c d d e e f f 10
  //   10 11 11 12 12 13 13 14 14 15 15 16 16 17 17 18 18 19 19 1a 1a 1b 1b 1c 0 0 1 1 2 2 3 3 0 0 1 1 2 2
  //   3 3 0 0 1 1 2 2 3 3 0 0 1 1 2 2 10*3 8*7 8*b 8*f 3 3 2 2 1 1 0 0 7 7 6 6 5 5 4 4 b b a a 9 9 8 8 f f
  //   e e d d c c 0 1 2 3 4 5 6 7 8 9 a b c d e f 0 1 2 3 4 5 6 7 8 9 a b c d e f 32*7 32*0 4 4 5 5 6 6 7
  //   7 8 8 9 9 a a b b c c d d e e f f 10 10 11 11 12 12 13 13 c c d d e e f f 10 10 11 11 12 12 13 13 14
  //   14 15 15 16 16 17 17 18 18 19 19 1a 1a 1b 1b 8*0 8*4 8*0 10*4 5 5 6 6 7 7 4 4 5 5 6 6 7 7 c c d d e
  //   e f f c c d d e e f f 4 4 5 5 6 6 7 7 0 0 1 1 2 2 3 3 c c d d e e f f 8 8 9 9 a a b b 0 1 2 3 4 5 6
  //   7 8 9 a b c d e f 0 1 2 3 4 5 6 7 8 9 a b c d e f 32*8 32*0 4 5 5 6 6 7 7 8 8 9 9 a a b b c c d d e
  //   e f f 10 10 11 11 12 12 13 13 14 b c c d d e e f f 10 10 11 11 12 12 13 13 14 14 15 15 16 16 17 17
  //   18 18 19 19 1a 1a 1b 8*0 8*4 8*0 10*4 5 5 6 6 7 7 4 4 5 5 6 6 7 7 c c d d e e f f c c d d e e f f 4
  //   4 5 5 6 6 7 7 0 0 1 1 2 2 3 3 c c d d e e f f 8 8 9 9 a a b b 0 1 2 3 4 5 6 7 8 9 a b c d e f 0 1 2
  //   3 4 5 6 7 8 9 a b c d e f 32*9 32*0 5 5 6 6 7 7 8 8 9 9 a a b b c c d d e e f f 10 10 11 11 12 12 13
  //   13 14 14 b b c c d d e e f f 10 10 11 11 12 12 13 13 14 14 15 15 16 16 17 17 18 18 19 19 1a 1a 0 0 1
  //   1 0 0 1 1 4 4 5 5 4 4 5 5 0 0 1 1 0 0 1 1 4 4 5 5 4 4 6*5 4*7 4*5 4*7 4*d 4*f 4*d 4*f 5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
endmodule
